// Logisim project Barramento.circ as structural Verilog: 1 circuit, main circuit main
module main (
  input  in_1,
  input  in_2,
  input  in_3,
  input  in_4,
  input  in_5,
  input  in_6,
  input  [7:0] in_7,
  input  in_8,
  output [7:0] out_9
);

  wire [7:0] register_1_q, register_2_q, register_3_q;

  Register register_1 (.D(out_9), .Q(register_1_q), .clk(in_3));  // open: en, clr
  Register register_2 (.D(out_9), .Q(register_2_q), .clk(in_6));  // open: en, clr
  assign out_9 = in_8 ? in_7 : 8'bz;  // Controlled_Buffer controlled_buffer_1
  assign out_9 = in_2 ? register_1_q : 8'bz;  // Controlled_Buffer controlled_buffer_2
  assign out_9 = in_5 ? register_2_q : 8'bz;  // Controlled_Buffer controlled_buffer_3
  assign out_9 = in_1 ? register_3_q : 8'bz;  // Controlled_Buffer controlled_buffer_4
  Register register_3 (.D(out_9), .Q(register_3_q), .clk(in_4));  // open: en, clr

  // Notes on the sheet:
  //   Nome: Rayssa Mara Caldini Costa
  //   Se tentar passar um valor diferente pelo barramento estando com um buffer com outra informação ativado, dará conflito
  //   Por exemplo: um registrador com valor 7 e outro com valor 4, se o buffer dos dois forem ativados, terá um conflito de informações
endmodule
