// Logisim project Memória 8 bits.circ as structural Verilog: 2 circuits, main circuit main
module main (
  input  [7:0] in_1,
  input  in_2,
  output [7:0] out_3
);

  RAM_1_bit ram_1_bit_1 (.Muda_o_valor(in_1[0]), .in_2(in_2), .out_3(out_3[0]));
  RAM_1_bit ram_1_bit_2 (.Muda_o_valor(in_1[1]), .in_2(in_2), .out_3(out_3[1]));
  RAM_1_bit ram_1_bit_3 (.Muda_o_valor(in_1[2]), .in_2(in_2), .out_3(out_3[2]));
  RAM_1_bit ram_1_bit_4 (.Muda_o_valor(in_1[3]), .in_2(in_2), .out_3(out_3[3]));
  RAM_1_bit ram_1_bit_5 (.Muda_o_valor(in_1[4]), .in_2(in_2), .out_3(out_3[4]));
  RAM_1_bit ram_1_bit_6 (.Muda_o_valor(in_1[5]), .in_2(in_2), .out_3(out_3[5]));
  RAM_1_bit ram_1_bit_7 (.Muda_o_valor(in_1[6]), .in_2(in_2), .out_3(out_3[6]));
  RAM_1_bit ram_1_bit_8 (.Muda_o_valor(in_1[7]), .in_2(in_2), .out_3(out_3[7]));

  // Notes on the sheet:
  //   Nome: Rayssa Mara Caldini Costa
  //   CI da RAM pra 8 bits
endmodule

module RAM_1_bit (
  input  Muda_o_valor,
  input  in_2,
  output out_3
);

  wire nand_1_out, nand_2_out, nand_4_out;

  nand nand_1 (nand_1_out, Muda_o_valor, in_2);
  nand nand_2 (nand_2_out, nand_1_out, in_2);
  nand nand_3 (out_3, nand_1_out, nand_4_out);
  nand nand_4 (nand_4_out, out_3, nand_2_out);

  // Notes on the sheet:
  //   Nome: Rayssa Mara Caldini Costa
  //   1 Bit de memória
  //   Habilita pra mudança de valor
endmodule
